# Fritzing sketch rotary8574 (saved by Fritzing 0.9.3b)
breadboards: 1

parts:
  U1 = PCF8574 [package="DIP16 [THT]"]
  Part1 = Arduino Uno (Rev3)
  R1 = Resistor [tolerance=±5% resistance=10k package=THT]
  R2 = Resistor [tolerance=±5% resistance=10k package=THT]
  S1 = Momentary Switch [package=ksa_sealed_tac_switch]
  RE1 = Rotary Encoder [package=THT]
  R3 = Resistor [tolerance=±5% resistance=220 package=THT]
  LED1 = LED - 3mm [color="Red (633nm)" package="3 mm [THT]"]
  S2 = Momentary Switch [package=ksa_sealed_tac_switch]

nets:
  GND: U1.A0, U1.A1, U1.A3, U1.GND, Part1.GND, S1.4, RE1.EncoderPinC, S2.1
  N1: U1.P0, S1.2
  N2: U1.P1, R3.Pin_1
  N3: U1.P2, RE1.EncoderPinA
  N4: U1.P3, RE1.EncoderPinB
  N5: U1.P4, S2.3
  N6: U1.SCL, Part1.A5/SCL, R2.Pin_1
  N7: U1.SDA, Part1.A4/SDA, R1.Pin_1
  VCC: U1.VCC, Part1.5V, R1.Pin_0, R2.Pin_0, LED1.anode
  N8: R3.Pin_0, LED1.cathode

notes:
  SDA and SCL from Arduino
  Notice 10K pull up resistors
  Interrupt
  pin
